# Fritzing sketch schematics (saved by Fritzing 0.9.3b)
breadboards: 1

parts:
  UNO = Arduino Uno (Rev3) - ICSP
  IC1 = L293D [package=THT]
  LEFT = DC Motor
  M1 = DC Motor
  Power_Supply = DC Power [voltage=7]
  IR_Sensor = TSOP312.., 314.. [package=THT]
  hc-sr1 = hc-sr04
  J1 = Basic Servo

nets:
  VCC: UNO.5V, IC1.+V, IR_Sensor.Vs, hc-sr1.VCC, J1.vcc
  N1: UNO.D8, IR_Sensor.Data
  N2: UNO.D9_PWM, J1.pulse
  N3: UNO.D10_PWM/SS, hc-sr1.Echo
  N4: UNO.D11_PWM/MOSI, hc-sr1.Trig
  GND: UNO.GND, IC1.0V, Power_Supply.V-, IR_Sensor.GND, hc-sr1.GND, J1.gnd
  N5: UNO.D2, IC1.In_1
  N6: UNO.D3_PWM, IC1.In_2
  N7: UNO.D4, IC1.Enable_1
  N8: UNO.D5_PWM, IC1.In_4
  N9: UNO.D6_PWM, IC1.In_3
  N10: UNO.D7, IC1.Enable_2
  N11: IC1.Out_1_(_Controlled_by_Enable_1_), LEFT.pin_2
  N12: IC1.Out_2_(_Controlled_by_Enable_1_), LEFT.pin_1
  N13: IC1.+Vmotor, Power_Supply.V+
  N14: IC1.Out_3_(_Controlled_by_Enable_2_), M1.pin_2
  N15: IC1.Out_4_(_Controlled_by_Enable_2_), M1.pin_1

custom parts:
  hc-sr04: This is a HC-SR04 Distance Sensor
